// Logisim project ass_1.circ as structural Verilog: 1 circuit, main circuit main
module main (
  input  D,
  input  B,
  input  A,
  input  c,
  output F___B_prime_D_prime___A_prime_BC_prime
);

  wire and_1_out, and_2_out, not_1_out, not_2_out, not_3_out, not_4_out;

  not not_1 (not_1_out, D);
  not not_2 (not_2_out, B);
  not not_3 (not_3_out, A);
  not not_4 (not_4_out, c);
  and and_1 (and_1_out, not_1_out, not_2_out);
  and and_2 (and_2_out, not_3_out, B, not_4_out);
  or or_1 (F___B_prime_D_prime___A_prime_BC_prime, and_1_out, and_2_out);
endmodule
