// Logisim project ass_2.circ as structural Verilog: 1 circuit, main circuit main
module main (
  input  MAIN_POWER___P,
  input  in_2,
  input  in_3,
  output out_4
);

  wire not_1_out;

  not not_1 (not_1_out, in_3);
  and and_1 (out_4, MAIN_POWER___P, in_2, not_1_out);

  // Notes on the sheet:
  //   WATER LEVEL ( L )
  //   TEMPERATURE ( T )
  //   PUMP OUTPUT ( Y )
endmodule
