// Logisim project ass_3.circ as structural Verilog: 1 circuit, main circuit main
module main (
  input  CLK,
  input  RST,
  input  CAR_DETECT,
  input  CAR_DIRECTION,
  input  PEDESTRIAN_REQ,
  output NS_RED,
  output NS_YELLOW,
  output [2:0] STATE_2_0,
  output NS_GREEN,
  output EW_RED,
  output EW_YELLOW,
  output EW_GREEN
);

  wire and_3_p2, NEXT_STATE_XOR_p2, or_1_p3, or_2_p2, or_4_p1, or_5_p2, undriven, undriven_2, undriven_3,
       undriven_4, undriven_5;
  wire [2:0] or_2_p4;

  // NOT_Gate not_1 has open pins: in=PEDESTRIAN_REQ, out=open
  // XOR_Gate NEXT_STATE_XOR: pin names not known; wires that end beside it: CAR_DIRECTION, NEXT_STATE_XOR_p2
  // AND_Gate and_1: pin names not known; wires that end beside it: CAR_DETECT, NEXT_STATE_XOR_p2
  // OR_Gate or_1: pin names not known; wires that end beside it: NEXT_STATE_XOR_p2, NEXT_STATE_XOR_p2, or_1_p3
  // XOR_Gate xor_1 is placed but not wired
  // AND_Gate and_2 is placed but not wired
  // OR_Gate or_2: pin names not known; wires that end beside it: or_1_p3, or_2_p2, or_2_p2, or_2_p4
  Register #(.width(3), .enable("true"), .reset("true"), .trigger("rising")) STATE_REGISTER (.Q(or_2_p4));  // open: D, en, clk, clr
  // NOT_Gate not_2 is placed but not wired
  // NOT_Gate not_3 is placed but not wired
  // NOT_Gate not_4 is placed but not wired
  // AND_Gate and_3: pin names not known; wires that end beside it: STATE_2_0, and_3_p2
  // AND_Gate and_4 has open pins: in1=undriven, out=open
  // AND_Gate and_5 has open pins: in1=undriven_2, out=open
  // AND_Gate and_6 has open pins: in1=undriven_3, out=open
  // AND_Gate and_7 has open pins: in1=undriven_4, out=open
  // AND_Gate and_8 has open pins: in1=undriven_5, out=open
  // OR_Gate or_3: pin names not known; wires that end beside it: and_3_p2, NS_YELLOW, NS_RED
  // OR_Gate or_4: pin names not known; wires that end beside it: or_4_p1, EW_RED, NS_GREEN
  // OR_Gate or_5: pin names not known; wires that end beside it: EW_YELLOW, or_5_p2, EW_GREEN
endmodule
