// Logisim project ass_4.circ as structural Verilog: 1 circuit, main circuit main
module main (
  input  Cin,
  input  X,
  input  Y,
  output S,
  output Cout
);

  wire and_1_out, and_2_out, xor_1_out;

  xor xor_1 (xor_1_out, X, Y);
  and and_1 (and_1_out, X, Y);
  xor xor_2 (S, Cin, xor_1_out);
  and and_2 (and_2_out, xor_1_out, Cin);
  xor xor_3 (Cout, and_2_out, and_1_out);
endmodule
