// Logisim project ass_5.circ as structural Verilog: 1 circuit, main circuit main
module main (
  output out_1,
  output out_2,
  output out_3,
  output out_4
);

  wire and_1_out, and_2_out, and_3_out, clock_1_out, undriven, undriven_2;

  Clock clock_1 (.out(clock_1_out));
  and and_1 (and_1_out, undriven, out_3, out_4, undriven_2);
  T_Flip_Flop t_ff_1 (.clk(clock_1_out), .T(and_1_out), .Q(out_3));  // open: Qn, preset, reset, en
  and and_2 (and_2_out, undriven, undriven_2);
  T_Flip_Flop t_ff_2 (.clk(clock_1_out), .T(and_2_out), .Q(out_4));  // open: Qn, preset, reset, en
  T_Flip_Flop t_ff_3 (.clk(clock_1_out), .T(and_3_out), .Q(out_1));  // open: Qn, preset, reset, en
  and and_3 (and_3_out, undriven, undriven, undriven_2);
  T_Flip_Flop t_ff_4 (.clk(clock_1_out), .T(1'b1), .Q(out_2));  // open: Qn, preset, reset, en
endmodule
