// Logisim project ass_6.circ as structural Verilog: 1 circuit, main circuit main
module main (
);

  Clock #(.labelVisible("true")) _1_Hz_CLOCK ();  // open: out
  Counter #(.width(4), .max(9), .labelVisible("true")) MOD_10_UNITS ();  // open: load, D, count, Q, carry, clk, clr
  Counter #(.width(3), .max(5), .labelVisible("true")) MOD_6_TENS ();  // open: load, D, count, Q, carry, clk, clr
endmodule
